// Logisim project Circuitos Aula.circ as structural Verilog
module main (
  input  in_1,
  input  in_2,
  input  [3:0] in_3,
  input  [3:0] in_4,
  output out_5,
  output [3:0] out_6
);

  and and_1 (out_5, in_1, in_2);
  assign out_6 = in_3 & in_4;  // AND_Gate and_2, 4 bits wide
endmodule

module Meio_Somador (
  input  A,
  input  B,
  output S,
  output COut
);

  xor xor_1 (S, A, B);
  and and_1 (COut, B, A);

  // Notes on the sheet:
  //   Meio Somador
endmodule

module Somador (
  input  Cin,
  input  A,
  input  B,
  output S,
  output Ts
);

  wire meio_somador_1_cout, meio_somador_1_s, meio_somador_2_cout;

  Meio_Somador meio_somador_1 (.A(A), .B(B), .S(meio_somador_1_s), .COut(meio_somador_1_cout));
  Meio_Somador meio_somador_2 (.A(Cin), .B(meio_somador_1_s), .S(S), .COut(meio_somador_2_cout));
  or or_1 (Ts, meio_somador_2_cout, meio_somador_1_cout);
endmodule

module Somador_4_bits (
  input  TE,
  input  A0,
  input  B0,
  input  A1,
  input  B1,
  input  A2,
  input  B2,
  input  A3,
  input  B3,
  output S1,
  output S2,
  output S3,
  output S4,
  output Carry_Out
);

  wire somador_1_ts, somador_2_ts, somador_3_ts;

  Somador somador_1 (.Cin(TE), .A(A0), .B(B0), .S(S1), .Ts(somador_1_ts));
  Somador somador_2 (.Cin(somador_1_ts), .A(A1), .B(B1), .S(S2), .Ts(somador_2_ts));
  Somador somador_3 (.Cin(somador_2_ts), .A(A2), .B(B2), .S(S3), .Ts(somador_3_ts));
  Somador somador_4 (.Cin(somador_3_ts), .A(A3), .B(B3), .S(S4), .Ts(Carry_Out));

  // Notes on the sheet:
  //   Somador de 4 Bits
endmodule

module Somador_8_Bits (
  input  Cin,
  input  A0,
  input  B0,
  input  A1,
  input  B1,
  input  A2,
  input  B2,
  input  A3,
  input  A4,
  input  B3,
  input  B4,
  input  A5,
  input  B5,
  input  A6,
  input  B6,
  input  A7,
  input  B7,
  output S0,
  output S1,
  output S2,
  output S3,
  output S4,
  output S5,
  output S6,
  output S7,
  output out_26
);

  wire somador_4_bits_1_carry_out;

  Somador_4_bits somador_4_bits_1 (
    .TE(Cin), .A0(A0), .B0(B0), .A1(A1), .B1(B1), .A2(A2), .B2(B2), .A3(A3), .B3(B3), .S1(S0), .S2(S1),
    .S3(S2), .S4(S3), .Carry_Out(somador_4_bits_1_carry_out));
  Somador_4_bits somador_4_bits_2 (
    .TE(somador_4_bits_1_carry_out), .A0(A4), .B0(B4), .A1(A5), .B1(B5), .A2(A6), .B2(B6), .A3(A7), .B3(B7),
    .S1(S4), .S2(S5), .S3(S6), .S4(S7), .Carry_Out(out_26));

  // Notes on the sheet:
  //   Somador de 8 Bits
  //   TS
  //   Overflow
endmodule

module Meio_Subtrator (
  input  A,
  input  B,
  output Diff,
  output Bout
);

  wire not_1_out;

  not not_1 (not_1_out, A);
  xor xor_1 (Diff, A, B);
  and and_1 (Bout, B, not_1_out);
endmodule

module Subtrator (
  input  Bin,
  input  A,
  input  B,
  output Diff,
  output Bout
);

  wire and_1_out, and_2_out, and_3_out, not_1_out, xor_2_out;

  not not_1 (not_1_out, A);
  xor xor_1 (Diff, Bin, xor_2_out);
  xor xor_2 (xor_2_out, A, B);
  and and_1 (and_1_out, Bin, not_1_out);
  and and_2 (and_2_out, not_1_out, B);
  and and_3 (and_3_out, B, Bin);
  or or_1 (Bout, and_1_out, and_2_out, and_3_out);

  // Notes on the sheet:
  //   ABar
  //   B
  //   Bin
  //   Diff
  //   Bout
endmodule

module Subtrator_4_bits (
  input  Bin,
  input  A0,
  input  B0,
  input  A1,
  input  B1,
  input  A2,
  input  B2,
  input  A3,
  input  B3,
  output Diff,
  output Diff_2,
  output Diff_3,
  output Diff_4,
  output Bout
);

  wire subtrator_1_bout, subtrator_2_bout, subtrator_3_bout;

  Subtrator subtrator_1 (.Bin(Bin), .A(A0), .B(B0), .Diff(Diff), .Bout(subtrator_1_bout));
  Subtrator subtrator_2 (.Bin(subtrator_1_bout), .A(A1), .B(B1), .Diff(Diff_2), .Bout(subtrator_2_bout));
  Subtrator subtrator_3 (.Bin(subtrator_2_bout), .A(A2), .B(B2), .Diff(Diff_3), .Bout(subtrator_3_bout));
  Subtrator subtrator_4 (.Bin(subtrator_3_bout), .A(A3), .B(B3), .Diff(Diff_4), .Bout(Bout));

  // Notes on the sheet:
  //   Bout
  //   Bout
  //   Bout
endmodule

module Subtrator_8_Bits (
  input  Bin,
  input  A0,
  input  B0,
  input  A1,
  input  B1,
  input  A2,
  input  B2,
  input  A3,
  input  B3,
  input  A4,
  input  B4,
  input  A5,
  input  B5,
  input  A6,
  input  B6,
  input  A7,
  input  B7,
  output S0,
  output S1,
  output S2,
  output S3,
  output S4,
  output S5,
  output S6,
  output S7,
  output Bout
);

  wire subtrator_4_bits_1_bout;

  Subtrator_4_bits subtrator_4_bits_1 (
    .Bin(Bin), .A0(A0), .B0(B0), .A1(A1), .B1(B1), .A2(A2), .B2(B2), .A3(A3), .B3(B3), .Diff(S0),
    .Diff_2(S1), .Diff_3(S2), .Diff_4(S3), .Bout(subtrator_4_bits_1_bout));
  Subtrator_4_bits subtrator_4_bits_2 (
    .Bin(subtrator_4_bits_1_bout), .A0(A4), .B0(B4), .A1(A5), .B1(B5), .A2(A6), .B2(B6), .A3(A7), .B3(B7),
    .Diff(S4), .Diff_2(S5), .Diff_3(S6), .Diff_4(S7), .Bout(Bout));

  // Notes on the sheet:
  //   Bout
endmodule

module Somador_Subtrator (
  input  Modo,
  input  A1,
  input  B1,
  input  A2,
  input  B2,
  input  A3,
  input  B3,
  input  A4,
  input  B4,
  output S1,
  output S2,
  output S3,
  output S4,
  output C4
);

  wire somador_1_ts, somador_2_ts, somador_3_ts, xor_1_out, xor_2_out, xor_3_out, xor_4_out;

  xor xor_1 (xor_1_out, Modo, B1);
  xor xor_2 (xor_2_out, Modo, B2);
  xor xor_3 (xor_3_out, Modo, B3);
  xor xor_4 (xor_4_out, Modo, B4);
  Somador somador_1 (.Cin(Modo), .A(A1), .B(xor_1_out), .S(S1), .Ts(somador_1_ts));
  Somador somador_2 (.Cin(somador_1_ts), .A(A2), .B(xor_2_out), .S(S2), .Ts(somador_2_ts));
  Somador somador_3 (.Cin(somador_2_ts), .A(A3), .B(xor_3_out), .S(S3), .Ts(somador_3_ts));
  Somador somador_4 (.Cin(somador_3_ts), .A(A4), .B(xor_4_out), .S(S4), .Ts(C4));

  // Notes on the sheet:
  //   A (0010) + B (0001) = 0001 (1 Carry)
endmodule

module Somador_Subtrator_1Bit (
  input  Modo,
  input  A1,
  input  B1,
  output S1,
  output C1
);

  wire xor_1_out;

  xor xor_1 (xor_1_out, Modo, B1);
  Somador somador_1 (.Cin(Modo), .A(A1), .B(xor_1_out), .S(S1), .Ts(C1));

  // Notes on the sheet:
  //   A (0010) + B (0001) = 0001 (1 Carry)
endmodule

module ULA (
  input  A,
  input  B,
  input  Modo,
  input  in_4,
  input  in_5,
  input  Seletor,
  input  Enable,
  input  [1:0] in_8,
  input  Enable_2,
  output out_10,
  output out_11
);

  wire A_B_out, AB_out, somador_subtrator_1_s1;

  Somador_Subtrator somador_subtrator_1 (
    .Modo(Modo), .A1(A), .B1(B), .S1(somador_subtrator_1_s1));  // open: A2, B2, A3, B3, A4, B4, S2, S3, S4, C4
  and AB (AB_out, A, B);
  or A_B (A_B_out, A, B);
  Multiplexer #(.select(2)) multiplexer_1 (
    .in0(somador_subtrator_1_s1), .in1(somador_subtrator_1_s1), .in2(AB_out), .in3(A_B_out), .out(out_11),
    .sel(in_8), .en(Enable_2));
  LED led_1 (.in(out_11));
  Multiplexer multiplexer_2 (.in0(in_4), .in1(in_5), .out(out_10), .sel(Seletor), .en(Enable));
  LED led_2 (.in(out_10));
endmodule

module ULA_Marvilhosa (
  input  A0,
  input  B0,
  input  Modo,
  input  [2:0] in_4,
  input  Enable,
  output Saida
);

  wire A_B_out, AB_out, Inversor_A_out, Inversor_B_out, not_1_out, Sempre_0_out, somador_subtrator_1bit_1_s1,
       xor_1_out;

  not not_1 (not_1_out, A0);
  and AB (AB_out, A0, B0);
  or A_B (A_B_out, A0, B0);
  xor xor_1 (xor_1_out, A0, B0);
  not Inversor_A (Inversor_A_out, A0);
  not Inversor_B (Inversor_B_out, B0);
  and Sempre_0 (Sempre_0_out, A0, not_1_out);
  Somador_Subtrator_1Bit somador_subtrator_1bit_1 (
    .Modo(Modo), .A1(B0), .B1(A0), .S1(somador_subtrator_1bit_1_s1));  // open: C1
  Multiplexer #(.select(3)) multiplexer_1 (
    .in0(somador_subtrator_1bit_1_s1), .in1(somador_subtrator_1bit_1_s1), .in2(AB_out), .in3(A_B_out),
    .in4(xor_1_out), .in5(Inversor_A_out), .in6(Inversor_B_out), .in7(Sempre_0_out), .out(Saida), .sel(in_4),
    .en(Enable));
  LED led_1 (.in(Saida));
endmodule

module ULA_4Bits (
  input  [3:0] A0,
  input  [3:0] B0,
  input  Modo,
  input  [2:0] Seletor,
  input  Enable,
  output Cout,
  output [3:0] Saida
);

  wire [3:0] A_B_out, AB_out, adder_1_out, bit_extender_1_out, Inversor_A_out, Inversor_B_out, not_1_out,
       Sempre_0_out, xor_1_out, xor_2_out;

  assign bit_extender_1_out = {{3{Modo}}, Modo};  // Bit_Extender bit_extender_1
  assign not_1_out = ~A0;  // NOT_Gate not_1, 4 bits wide
  assign xor_1_out = bit_extender_1_out ^ B0;  // XOR_Gate xor_1, 4 bits wide
  assign AB_out = A0 & B0;  // AND_Gate AB, 4 bits wide
  assign A_B_out = A0 | B0;  // OR_Gate A_B, 4 bits wide
  assign xor_2_out = A0 ^ B0;  // XOR_Gate xor_2, 4 bits wide
  assign Inversor_A_out = ~A0;  // NOT_Gate Inversor_A, 4 bits wide
  assign Inversor_B_out = ~B0;  // NOT_Gate Inversor_B, 4 bits wide
  assign Sempre_0_out = A0 & not_1_out;  // AND_Gate Sempre_0, 4 bits wide
  Adder #(.width(4)) adder_1 (.a(A0), .b(xor_1_out), .out(adder_1_out), .cin(Modo), .cout(Cout));
  Multiplexer #(.select(3), .width(4)) multiplexer_1 (
    .in0(adder_1_out), .in1(adder_1_out), .in2(AB_out), .in3(A_B_out), .in4(xor_2_out), .in5(Inversor_A_out),
    .in6(Inversor_B_out), .in7(Sempre_0_out), .out(Saida), .sel(Seletor), .en(Enable));
endmodule

module ULA_8Bits (
  input  [7:0] A0,
  input  [7:0] B0,
  input  Modo,
  input  [2:0] in_4,
  input  Enable,
  output out_6,
  output [7:0] out_7
);

  wire [7:0] A_B_out, AB_out, adder_1_out, bit_extender_1_out, Inversor_A_out, Inversor_B_out, not_1_out,
       Sempre_0_out, xor_1_out, xor_2_out;

  assign not_1_out = ~A0;  // NOT_Gate not_1, 8 bits wide
  assign bit_extender_1_out = {{7{Modo}}, Modo};  // Bit_Extender bit_extender_1
  assign AB_out = A0 & B0;  // AND_Gate AB, 8 bits wide
  assign A_B_out = A0 | B0;  // OR_Gate A_B, 8 bits wide
  assign xor_1_out = A0 ^ B0;  // XOR_Gate xor_1, 8 bits wide
  assign Inversor_A_out = ~A0;  // NOT_Gate Inversor_A, 8 bits wide
  assign Inversor_B_out = ~B0;  // NOT_Gate Inversor_B, 8 bits wide
  assign Sempre_0_out = A0 & not_1_out;  // AND_Gate Sempre_0, 8 bits wide
  assign xor_2_out = bit_extender_1_out ^ B0;  // XOR_Gate xor_2, 8 bits wide
  Adder adder_1 (.a(A0), .b(xor_2_out), .out(adder_1_out), .cin(Modo), .cout(out_6));
  Multiplexer #(.select(3), .width(8)) multiplexer_1 (
    .in0(adder_1_out), .in1(adder_1_out), .in2(AB_out), .in3(A_B_out), .in4(xor_1_out), .in5(Inversor_A_out),
    .in6(Inversor_B_out), .in7(Sempre_0_out), .out(out_7), .sel(in_4), .en(Enable));
endmodule

module Registrador (
  input  [3:0] A
);

  wire clock_1_out;
  wire [3:0] register_1_q;

  Register #(.width(4)) register_1 (.D(A), .en(1'b1), .Q(register_1_q), .clk(clock_1_out), .clr(1'b0));
  Clock clock_1 (.out(clock_1_out));
  Hex_Digit_Display hex_digit_display_1 (.value(register_1_q));  // open: dp

  // Notes on the sheet:
  //   Enable
  //   Clock
  //   Clear
  //   Display Hexadecimal
endmodule

module ULA___Registrador (
  input  [3:0] A,
  input  [3:0] B,
  input  Clear,
  input  Clear_2,
  input  Modo,
  input  [2:0] Seletor,
  output [3:0] Saida,
  output Cout
);

  wire Clock_out;
  wire [3:0] register_1_q, register_2_q;

  Clock Clock (.out(Clock_out));
  Register #(.width(4)) register_1 (.D(A), .en(1'b1), .Q(register_1_q), .clk(Clock_out), .clr(Clear));
  ULA_4Bits ula_4bits_1 (
    .Seletor(Seletor), .A0(register_1_q), .B0(register_2_q), .Modo(Modo), .Cout(Cout), .Saida(Saida),
    .Enable(1'b1));
  Register #(.width(4)) register_2 (.D(B), .en(1'b1), .Q(register_2_q), .clk(Clock_out), .clr(Clear_2));
  Hex_Digit_Display hex_digit_display_1 (.value(Saida));  // open: dp

  // Notes on the sheet:
  //   Enable
  //   Enable
  //   Enable
endmodule

module Acumulador (
  input  [3:0] A,
  input  Modo,
  input  [2:0] Seletor,
  input  Clear,
  output Cout
);

  wire Clock_out;
  wire [3:0] register_1_q, ula_4bits_1_saida;

  ULA_4Bits ula_4bits_1 (
    .Seletor(Seletor), .A0(A), .B0(register_1_q), .Modo(Modo), .Cout(Cout), .Saida(ula_4bits_1_saida),
    .Enable(1'b1));
  Hex_Digit_Display hex_digit_display_1 (.value(ula_4bits_1_saida));  // open: dp
  Clock Clock (.out(Clock_out));
  Register #(.width(4)) register_1 (.D(ula_4bits_1_saida), .en(1'b1), .Q(register_1_q), .clk(Clock_out), .clr(Clear));
  Hex_Digit_Display hex_digit_display_2 (.value(register_1_q));  // open: dp

  // Notes on the sheet:
  //   Enable
  //   Enable
endmodule

module Acumulador2 (
  input  [3:0] A,
  input  [3:0] B,
  input  Modo,
  input  [2:0] Seletor,
  input  Clear,
  input  Modo_2,
  input  [2:0] Seletor_2,
  input  Cout,
  output Cout_2,
  output [3:0] Saida_Final
);

  wire Clock_out;
  wire [3:0] register_1_q, ula_4bits_1_saida;

  ULA_4Bits ula_4bits_1 (
    .Seletor(Seletor), .A0(A), .B0(B), .Modo(Modo), .Cout(Cout_2), .Saida(ula_4bits_1_saida), .Enable(1'b1));
  Hex_Digit_Display hex_digit_display_1 (.value(ula_4bits_1_saida));  // open: dp
  Clock Clock (.out(Clock_out));
  ULA_4Bits ula_4bits_2 (
    .Seletor(Seletor_2), .A0(ula_4bits_1_saida), .B0(register_1_q), .Modo(Modo_2), .Cout(Cout),
    .Saida(Saida_Final), .Enable(1'b1));
  Register #(.width(4)) register_1 (.D(ula_4bits_1_saida), .en(1'b1), .Q(register_1_q), .clk(Clock_out), .clr(Clear));
  Hex_Digit_Display hex_digit_display_2 (.value(Saida_Final));  // open: dp
  Hex_Digit_Display hex_digit_display_3 (.value(register_1_q));  // open: dp

  // Notes on the sheet:
  //   Enable
  //   Saida 1
  //   Enable
  //   Enable
  //   Acumulador
endmodule

module Acumulador_c__Multiplex (
  input  Acumulador,
  input  [3:0] A,
  input  [3:0] B,
  input  Clear,
  input  Clear_2,
  input  Modo,
  input  [2:0] Seletor,
  input  Clear_3,
  input  Acumulador_2,
  input  [3:0] A_2,
  input  [3:0] B_2,
  input  Clear_4,
  input  Clear_5,
  input  Modo_2,
  input  [2:0] Seletor_2,
  input  Clear_6,
  output [3:0] Saida,
  output Cout,
  output [3:0] Saida_2,
  output Cout_2
);

  wire clock_1_out, clock_2_out, undriven;
  wire [3:0] multiplexer_1_out, multiplexer_2_out, Reg_A_q, Reg_B_q, registrador_com_flip_flop_1_saida,
       registrador_com_flip_flop_2_saida, ula_4bits_1_saida, ula_4bits_2_saida;

  Hex_Digit_Display hex_digit_display_1 (.value(Reg_A_q));  // open: dp
  Hex_Digit_Display hex_digit_display_2 (.value(registrador_com_flip_flop_1_saida));  // open: dp
  Clock clock_1 (.out(clock_1_out));
  Clock clock_2 (.out(clock_2_out));
  Register #(.width(4)) Reg_A (.D(A), .en(1'b1), .Q(Reg_A_q), .clk(clock_1_out), .clr(Clear));
  Registrador_com_Flip_Flop registrador_com_flip_flop_1 (
    .Clock(clock_2_out), .Entrada(A_2), .Clear(Clear_4), .Saida(registrador_com_flip_flop_1_saida));
  Multiplexer #(.width(4)) multiplexer_1 (
    .in0(Reg_A_q), .in1(Saida), .out(multiplexer_1_out), .sel(Acumulador));  // open: en
  Multiplexer #(.width(4)) multiplexer_2 (
    .in0(registrador_com_flip_flop_1_saida), .in1(Saida_2), .out(multiplexer_2_out), .sel(Acumulador_2),
    .en(undriven));
  ULA_4Bits ula_4bits_1 (
    .Seletor(Seletor), .A0(multiplexer_1_out), .B0(Reg_B_q), .Modo(Modo), .Cout(Cout),
    .Saida(ula_4bits_1_saida), .Enable(1'b1));
  ULA_4Bits ula_4bits_2 (
    .Seletor(Seletor_2), .A0(multiplexer_2_out), .B0(registrador_com_flip_flop_2_saida), .Modo(Modo_2),
    .Cout(Cout_2), .Saida(ula_4bits_2_saida), .Enable(1'b1));
  Register #(.width(4)) Reg_B (.D(B), .en(1'b1), .Q(Reg_B_q), .clk(clock_1_out), .clr(Clear_2));
  Register #(.width(4)) ACC (.D(ula_4bits_1_saida), .en(1'b1), .Q(Saida), .clk(clock_1_out), .clr(Clear_3));
  Registrador_com_Flip_Flop registrador_com_flip_flop_2 (
    .Clock(clock_2_out), .Entrada(B_2), .Clear(Clear_5), .Saida(registrador_com_flip_flop_2_saida));
  Registrador_com_Flip_Flop registrador_com_flip_flop_3 (
    .Clock(clock_2_out), .Entrada(ula_4bits_2_saida), .Clear(Clear_6), .Saida(Saida_2));
  Hex_Digit_Display hex_digit_display_3 (.value(Saida));  // open: dp
  Hex_Digit_Display hex_digit_display_4 (.value(Saida_2));  // open: dp
  Hex_Digit_Display hex_digit_display_5 (.value(Reg_B_q));  // open: dp
  Hex_Digit_Display hex_digit_display_6 (.value(registrador_com_flip_flop_2_saida));  // open: dp

  // Notes on the sheet:
  //   Reg A
  //   Reg A
  //   Enable
  //   Enable
  //   Enable
  //   Enable
  //   Enable
  //   Acumulado
  //   Acumulado
  //   Reg B
  //   Reg B
endmodule

module Registrador_com_Flip_Flop (
  input  Clock,
  input  Clear,
  input  [3:0] Entrada,
  output [3:0] Saida
);

  D_Flip_Flop d_ff_1 (.clk(Clock), .D(Entrada[0]), .Q(Saida[0]), .preset(1'b0), .en(1'b1), .reset(Clear));  // open: Qn
  D_Flip_Flop d_ff_2 (.clk(Clock), .D(Entrada[1]), .Q(Saida[1]), .preset(1'b0), .en(1'b1), .reset(Clear));  // open: Qn
  D_Flip_Flop d_ff_3 (.clk(Clock), .D(Entrada[2]), .Q(Saida[2]), .preset(1'b0), .en(1'b1), .reset(Clear));  // open: Qn
  D_Flip_Flop d_ff_4 (.clk(Clock), .D(Entrada[3]), .Q(Saida[3]), .preset(1'b0), .en(1'b1), .reset(Clear));  // open: Qn

  // Notes on the sheet:
  //   Preset
  //   Enable
endmodule

module Flip_Flop_D (
  input  D,
  input  Clock,
  input  Clock_2,
  input  D0,
  input  Enable,
  output Q,
  output Q_Inverso,
  output Q_Inverso_2
);

  wire nand_2_out, nand_3_out, nand_6_out, nand_7_out, nand_8_out, not_1_out;

  not not_1 (not_1_out, D);
  nand nand_1 (Clock_2, D0, D0);
  nand nand_2 (nand_2_out, D, Clock);
  nand nand_3 (nand_3_out, not_1_out, Clock);
  nand nand_4 (Q, nand_2_out, Q_Inverso);
  nand nand_5 (Q_Inverso, Q, nand_3_out);
  nand nand_6 (nand_6_out, D0, Enable);
  nand nand_7 (nand_7_out, Enable, Clock_2);
  nand nand_8 (nand_8_out, nand_6_out, Q_Inverso_2);
  nand nand_9 (Q_Inverso_2, nand_8_out, nand_7_out);
endmodule

module FlipFlop___Reg_do_Zero (
  input  Clock,
  input  D0,
  input  D1,
  input  D2,
  input  D3,
  output Q_Inverso,
  output Q_Inverso_2,
  output [3:0] Q,
  output Q_Inverso_3,
  output Q_Inverso_4
);

  wire nand_1_out, nand_2_out, nand_3_out, nand_4_out, nand_5_out, nand_6_out, nand_7_out, nand_8_out,
       not_1_out, not_2_out, not_3_out, not_4_out;

  not not_1 (not_1_out, D0);
  not not_2 (not_2_out, D1);
  not not_3 (not_3_out, D2);
  not not_4 (not_4_out, D3);
  nand nand_1 (nand_1_out, D0, Clock);
  nand nand_2 (nand_2_out, not_1_out, Clock);
  nand nand_3 (nand_3_out, D1, Clock);
  nand nand_4 (nand_4_out, not_2_out, Clock);
  nand nand_5 (nand_5_out, D2, Clock);
  nand nand_6 (nand_6_out, not_3_out, Clock);
  nand nand_7 (nand_7_out, D3, Clock);
  nand nand_8 (nand_8_out, not_4_out, Clock);
  nand nand_9 (Q[0], nand_1_out, Q_Inverso);
  nand nand_10 (Q_Inverso, Q[0], nand_2_out);
  nand nand_11 (Q[1], nand_3_out, Q_Inverso_2);
  nand nand_12 (Q_Inverso_2, Q[1], nand_4_out);
  nand nand_13 (Q[2], nand_5_out, Q_Inverso_3);
  nand nand_14 (Q_Inverso_3, Q[2], nand_6_out);
  nand nand_15 (Q[3], nand_7_out, Q_Inverso_4);
  nand nand_16 (Q_Inverso_4, Q[3], nand_8_out);
endmodule

module Program_Counter__PC (
  input  Clear,
  input  Clock,
  input  Cin,
  input  Cout,
  output [3:0] Saida
);

  wire [3:0] registrador_com_flip_flop_1_saida;

  Hex_Digit_Display hex_digit_display_1 (.value(registrador_com_flip_flop_1_saida));  // open: dp
  Registrador_com_Flip_Flop registrador_com_flip_flop_1 (
    .Clock(Clock), .Entrada(Saida), .Clear(Clear), .Saida(registrador_com_flip_flop_1_saida));
  Adder #(.width(4)) adder_1 (.a(registrador_com_flip_flop_1_saida), .b(4'b0001), .out(Saida), .cin(Cin), .cout(Cout));
  Hex_Digit_Display hex_digit_display_2 (.value(Saida));  // open: dp

  // Notes on the sheet:
  //   Entrada = Saida do Somador
  //   Saida Registrador
  //   Contador +1
  //   Saida PC
endmodule

module ROM (
  input  [3:0] Entrada,
  output [3:0] Saida
);

  ROM_part #(.addrWidth(4), .dataWidth(4)) rom_1 (.addr(Entrada), .data(Saida));  // open: sel
  Hex_Digit_Display hex_digit_display_1 (.value(Saida));  // open: dp

  // Notes on the sheet:
  //   contents of rom_1 (hex, n*v repeats v):
  //   1 2 3 4 5 6 7 8 9 a b c d e f
  //   Valor Saida
endmodule

module ROM___Program_Counter__PC (
  input  Clear,
  input  Cin,
  input  Cout,
  output [3:0] out_4
);

  wire Clock_out;
  wire [3:0] program_counter_pc_1_saida;

  Clock Clock (.out(Clock_out));
  Program_Counter__PC program_counter_pc_1 (
    .Clock(Clock_out), .Clear(Clear), .Cin(Cin), .Cout(Cout), .Saida(program_counter_pc_1_saida));
  Hex_Digit_Display hex_digit_display_1 (.value(out_4));  // open: dp
  ROM rom_1 (.Entrada(program_counter_pc_1_saida), .Saida(out_4));

  // Notes on the sheet:
  //   PC
  //   ROM
endmodule
